# Fritzing sketch Roomba_Wiring (saved by Fritzing 0.9.4)

parts:
  Q1 = PNP-Transistor [package="TO92 [THT]"]
  U3 = DIN7 [package=din7]  # not connected
  U4 = ISL29102 [package=odfn6]
  U5 = Buck Converter [package=odfn6]
  WeMos_D1_Mini1 = WeMos D1 Mini

nets:
  N1: Q1.E, U4.VOUT, U5.ESP_-, WeMos_D1_Mini1.G
  N2: Q1.C, WeMos_D1_Mini1.D3
  N3: U4.NC, U5.Roomba_+
  N4: U4.REXT, U5.Roomba_-, WeMos_D1_Mini1.5V

notes:
  PNP
  Transistor
  Wemos D1 Mini
  Roomba
  OI Port
  Step down converter
  Out
  5v
  In
  18v
